# Fritzing sketch 2DCmotor (saved by Fritzing 0.9.3b)
circuit board: 10cm x 6cm

parts:
  Part1 = Arduino Uno (Rev3)
  M1 = DC Motor
  M2 = DC Motor
  Power_plug1 = Power plug
  L298N1 = H-Bridge L298N DC motor driver

nets:
  GND: Part1.GND, Power_plug1.GND, L298N1.GND
  N1: Part1.D4, L298N1.IN4
  N2: Part1.D5_PWM, L298N1.IN3
  N3: Part1.D6_PWM, L298N1.IN2
  N4: Part1.D7, L298N1.IN1
  5V: Part1.5V, L298N1.5V
  N5: M1.pin_1, L298N1.OUT2
  N6: M1.pin_2, L298N1.OUT1
  N7: M2.pin_1, L298N1.OUT4
  N8: M2.pin_2, L298N1.OUT3
  VCC: Power_plug1.VCC, L298N1.12V
  N9: L298N1.ENA, L298N1.ENA-5V
  N10: L298N1.ENB, L298N1.ENB-5V

notes:
  L298N Motor Driver Board
  Left Motor
  Right Motor
  Power Supply - 12v

custom parts:
  H-Bridge L298N DC motor driver: 2x DC motor driver with 78M05 positive voltage regulator (7..35 V) L298N: max 46 V, 2 A Set 5 V Enable jumper to enable 5 V regultor (needed for the L298N) and +5 V output at screw terminal or supply external +5 V at screw terminal Set ENA and/or ENB to +5 V to enable motor permanently or supply ENA and/or ENB with PWM signal IN1 and IN2 set rotation directory for motor A (OUT1/OUT2) IN2 and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
