# Fritzing sketch 2Servomotor (saved by Fritzing 0.9.3b)
circuit board: 10cm x 6cm

parts:
  Part1 = Arduino Uno (Rev3)
  J1 = Basic Servo
  J2 = Basic Servo

nets:
  GND: Part1.GND, J1.gnd, J2.gnd
  N1: Part1.D5_PWM, J1.pulse
  N2: Part1.D6_PWM, J2.pulse
  VCC: Part1.5V, J1.vcc, J2.vcc

notes:
  L298N Motor Driver Board
  Motor 2
  Motor 1
