# Fritzing sketch 2Steppermotor (saved by Fritzing 0.9.3b)
circuit board: 10cm x 6cm
breadboards: 1

parts:
  Part1 = Arduino Uno (Rev3)
  M1 = Stepper Motor - Bipolar
  M2 = Stepper Motor - Bipolar
  Power_plug1 = Power plug
  DRV_1 = DRV 8825 Stepper Motor Carrier, High Current [part_number="DRV 8825"]
  DRV_2 = DRV 8825 Stepper Motor Carrier, High Current [part_number="DRV 8825"]

nets:
  N1: Part1.D8, DRV_1.ENABLE, DRV_2.ENABLE
  N2: Part1.GND, DRV_1.GROUND_LOG, DRV_2.GROUND_LOG
  N3: Part1.D4, DRV_1.STEP
  N4: Part1.D5_PWM, DRV_2.STEP
  N5: Part1.D6_PWM, DRV_1.DIRECTION
  N6: Part1.D7, DRV_2.DIRECTION
  N7: Part1.5V, DRV_1.VOLTAGE_DD, DRV_2.VOLTAGE_DD
  N8: M1.A, DRV_1.OUT_2B
  N9: M1.C, DRV_1.OUT_2A
  N10: M1.B, DRV_1.OUT_1A
  N11: M1.D, DRV_1.OUT_1B
  N12: M2.A, DRV_2.OUT_2B
  N13: M2.C, DRV_2.OUT_2A
  N14: M2.B, DRV_2.OUT_1A
  N15: M2.D, DRV_2.OUT_1B
  N16: Power_plug1.GND, DRV_1.GROUND_ST/_MT, DRV_2.GROUND_ST/_MT
  N17: Power_plug1.VCC, DRV_1.VOLTAGE_ST/_MT, DRV_2.VOLTAGE_ST/_MT

notes:
  L298N Motor Driver Board
  Motor 2
  Motor 1
